# Fritzing sketch Airsensor (saved by Fritzing 0.9.10b)
circuit board: 8.46667cm x 5.64444cm
breadboards: 1

parts:
  Part1 = Arduino Nano RP2040
  Part2 = SCD30
  Part3 = Adafruit BME680 [part_number="Adafruit #3660"]

nets:
  N1: Part1.RESET, Part1.A7
  GND: Part1.GND, Part1.D13~, Part2.GND, Part3.GND
  N2: Part1.D11/MOSI, Part1.+5V
  N3: Part1.A5, Part2.TX/SCL, Part3.SCK/SCL
  N4: Part1.A4, Part2.RX/SDA, Part3.SDI/SDA
  3V3: Part1.3V3, Part2.VDD, Part3.VCC

custom parts:
  Arduino Nano RP2040: At the core of the Arduino Nano RP2040 Connect is the Raspberry Pi RP2040; a dual-core Arm Cortex M0+ processor, with the on-board ESP32 being available as a co-processor. There’s 16MB of flash memory that’s off-chip, providing plenty of room for code and storage. The highly adaptable u-blox NINA-W102 WiFi and Bluetooth radio module provides connectivity, allowing the device to harness the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
  SCD30: CO2 , humidity, and temperature sensor * Current consumption: 19 mA @ 1 meas. per 2 s. * Digital interface UART or I2C * Company: Sensirion - The Sensor Company Electrical specifications * average current: 19 mA * max. current: 75 mA * DC supply: 3.3 V - 5.5 V Operation conditions * temperature: 0 – 50°C * humidity: 0 – 95 %RH * sensor lifetime: 15 years CO2-sensor: * NDIR CO 2 sensor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
